# Fritzing sketch Schematics (saved by Fritzing 0.8.5b)
breadboards: 1

parts:
  Part1 = Arduino Nano (Rev3.0)
  U1 = RELAY [package=relay-g5q]
  U2 = RELAY [package=relay-g5q]
  U3 = RELAY [package=relay-g5q]

nets:
  N1: Part1.D5, U1.COIL1
  N2: Part1.D6, U2.COIL1
  N3: Part1.D7, U3.COIL1
  GND: U1.COIL2, U2.COIL2, U3.COIL2
